# Fritzing sketch Tegninger (saved by Fritzing 0.9.9b)
breadboards: 1

parts:
  Part3 = Arduino Motor Shield (Rev3)
  Part4 = Arduino Uno (Rev3)  # not connected
  VCC1 = 4 x AAA Battery Mount
  M2 = DC Motor
  M1 = DC Motor
  U1 = 74HC595 [package="DIP16 [THT]"]
  IC1 = IC, DIP package, 16 pins [chip_label=CD4051BE]
  S2 = Round Pushbutton
  S3 = Round Pushbutton
  S4 = Round Pushbutton
  S5 = Round Pushbutton
  S6 = Round Pushbutton
  S1 = Pushbutton [package="[THT]"]
  R1 = Resistor [tolerance=±5% resistance=110 package="0603 [SMD]"]
  R2 = Resistor [tolerance=±5% resistance=110 package="0603 [SMD]"]
  R3 = Resistor [tolerance=±5% resistance=110 package="0603 [SMD]"]
  R4 = Resistor [tolerance=±5% resistance=110 package="0603 [SMD]"]
  R5 = Resistor [tolerance=±5% resistance=110 package="0603 [SMD]"]
  R6 = Resistor [tolerance=±5% resistance=110 package="0603 [SMD]"]
  R7 = Resistor [tolerance=±5% resistance=110 package="0603 [SMD]"]
  LED1 = LEDs [package=led10mm]
  LED2 = LEDs [package=led10mm]
  LED3 = LEDs [package=led10mm]
  LED4 = LEDs [package=led10mm]
  LED5 = LEDs [package=led10mm]
  LED6 = LEDs [package=led10mm]
  LED7 = LEDs [package=led10mm]
  R8 = Resistor [tolerance=±5% resistance=110 package="0603 [SMD]"]
  R9 = Resistor [tolerance=±5% resistance=110 package="0603 [SMD]"]
  R10 = Resistor [tolerance=±5% resistance=2.2k package="0603 [SMD]"]
  R11 = Resistor [tolerance=±5% resistance=2.2k package="0603 [SMD]"]
  Q1 = QRD1114 [package=qrd1114]
  Q2 = QRD1114 [package=qrd1114]

nets:
  N1: Part3.A5, IC1.pin11
  N2: Part3.D8/BreakeB, IC1.pin3
  N3: Part3.D9/BreakeA, IC1.pin2
  N4: Part3.D10_PWM, IC1.pin1
  N5: Part3.D2, R10.Pin_1, Q2.C
  N6: Part3.D4, U1.ST_CP
  N7: Part3.D5_PWM, U1.SH_CP
  N8: Part3.D6_PWM, R11.Pin_0, Q1.C
  N9: Part3.D7, U1.DS
  N10: Part3.B-, M2.pin_2
  N11: Part3.B+, M2.pin_1
  N12: Part3.A-, M1.pin_2
  N13: Part3.A+, M1.pin_1
  N14: Part3.VMOT, VCC1.+
  GND: Part3.GND, VCC1.-, U1.GND, U1.OE, IC1.pin14, IC1.pin15, IC1.pin16, S2.leg0, S3.leg0, S4.leg0, S5.leg0, S6.leg0, S1.Pin_3, S1.Pin_4, R1.Pin_0, R2.Pin_0, R3.Pin_0, R4.Pin_0, R5.Pin_0, R6.Pin_0, R7.Pin_0, Q1.E, Q1.K, Q2.E, Q2.K
  5V: Part3.5V, U1.MR, U1.VCC, IC1.pin8, R8.Pin_0, R9.Pin_1, R10.Pin_0, R11.Pin_1
  N15: U1.Q1, LED7.A
  N16: U1.Q2, LED6.A
  N17: U1.Q3, LED5.A
  N18: U1.Q4, LED4.A
  N19: U1.Q5, LED3.A
  N20: U1.Q6, LED2.A
  N21: U1.Q7, LED1.A
  N22: IC1.pin4, S5.leg1
  N23: IC1.pin5, S2.leg1
  N24: IC1.pin6, S3.leg1
  N25: IC1.pin7, S4.leg1
  N26: IC1.pin9, S1.Pin_1, S1.Pin_2
  N27: IC1.pin13, S6.leg1
  N28: R1.Pin_1, LED6.C
  N29: R2.Pin_1, LED4.C
  N30: R3.Pin_1, LED2.C
  N31: R4.Pin_1, LED1.C
  N32: R5.Pin_1, LED3.C
  N33: R6.Pin_1, LED5.C
  N34: R7.Pin_1, LED7.C
  N35: R8.Pin_1, Q2.A
  N36: R9.Pin_0, Q1.A

// code stored in the sketch: Untitled.ino

